# Fritzing sketch HolonomicDrive-Fall2019 (saved by Fritzing 0.9.3b)

parts:
  Part1 = Arduino Uno (Rev3)
  Front_Right = DC Motor
  J1 = Basic Servo
  VCC1 = Battery  # not connected
  Rear_Right = DC Motor
  Left_Rear = DC Motor
  Left_Front = DC Motor
  Mod1 = Talon SRX
  Mod2 = Talon SRX
  Mod3 = Talon SRX
  Mod4 = Talon SRX
  20A_Circuit_Breaker = Fuse with Handler [part_number=Htc-15m]  # not connected
  20A_Circuit_Breaker_2 = Fuse with Handler [part_number=Htc-15m]  # not connected
  10A_Fuse = Fuse with Handler [part_number=Htc-15m]  # not connected
  20A_Circuit_Breaker_3 = Fuse with Handler [part_number=Htc-15m]  # not connected
  20A_Circuit_Breaker_4 = Fuse with Handler [part_number=Htc-15m]  # not connected
  U1 = RF-LINK_RX [package=rf-link_rx]  # not connected

nets:
  N1: Part1.D9_PWM, Mod1.CAN1_Y, Mod1.CAN1_G
  N2: Part1.D10_PWM/SS, Mod4.CAN1_Y
  N3: Part1.D11_PWM/MOSI, Mod3.CAN1_Y
  N4: Part1.D3_PWM, Mod2.CAN1_Y
  N5: Part1.D5_PWM, J1.pulse
  N6: Front_Right.pin_1, Mod1.M-
  N7: Front_Right.pin_2, Mod1.M+
  N8: Rear_Right.pin_1, Mod2.M-
  N9: Rear_Right.pin_2, Mod2.M+
  N10: Left_Rear.pin_1, Mod4.M-
  N11: Left_Rear.pin_2, Mod4.M+
  N12: Left_Front.pin_1, Mod3.M-
  N13: Left_Front.pin_2, Mod3.M+
